# Fritzing sketch jarvis (saved by Fritzing 0.9.2b)
breadboards: 1

parts:
  DS2 = DS18B20 1-Wire Temperature Sensor Probe Cable
  THERMO1 = MAX31855 Breakout Board with Thermocouple
  LED1 = smd LED [color="Red (633nm)" package="0805 [SMD]"]
  LED2 = smd LED [color="Green (560nm)" package="0805 [SMD]"]
  LED3 = smd LED [color="Blue (525nm)" package="0805 [SMD]"]
  Raspberry_Pi1 = Raspberry Pi 2
  R1 = Resistor [tolerance=±5% resistance=4.7k package="0402 [SMD]"]
  R3 = Resistor [tolerance=±5% resistance=220 package="0402 [SMD]"]
  R4 = Resistor [tolerance=±5% resistance=220 package="0402 [SMD]"]
  R5 = Resistor [tolerance=±5% resistance=220 package="0402 [SMD]"]
  SW1 = PowerSwitch Tail II

nets:
  GND: DS2.GND, THERMO1.GND, Raspberry_Pi1.GND, R3.Pin_1, R4.Pin_1, R5.Pin_1, SW1.-in
  VDD: DS2.VDD, THERMO1.Vin, Raspberry_Pi1.3v3, R1.Pin_0
  N1: DS2.shield, Raspberry_Pi1.GPIO4, R1.Pin_1
  N2: THERMO1.DO, Raspberry_Pi1.GPIO18
  N3: THERMO1.CS, Raspberry_Pi1.GPIO24
  N4: THERMO1.CLK, Raspberry_Pi1.GPIO25
  N5: LED1.cathode, R5.Pin_0
  N6: LED1.anode, Raspberry_Pi1.GPIO23, SW1.+in
  N7: LED2.cathode, R3.Pin_0
  N8: LED2.anode, Raspberry_Pi1.GPIO16
  N9: LED3.cathode, R4.Pin_0
  N10: LED3.anode, Raspberry_Pi1.GPIO21
